// Logisim project main.circ as structural Verilog: 8 circuits, main circuit main
module main (
);

  wire summator_subtractor_1_s0;

  summator_subtractor summator_subtractor_1 (
    .a3(summator_subtractor_1_s0), .s0(summator_subtractor_1_s0));  // open: op, a0, a1, a2, a4, a5, a6, a7, b0, b1, b2, b3, b4, b5, b6, b7, Overflow, s1, s2, s3, s4, s5, s6, s7
endmodule

module summator (
  input  a0,
  input  b0,
  input  c0,
  input  a1,
  input  b1,
  input  a2,
  input  b2,
  input  a3,
  input  b3,
  input  a4,
  input  b4,
  input  a5,
  input  b5,
  input  a6,
  input  b6,
  input  a7,
  input  b7,
  output s0,
  output s1,
  output s2,
  output s3,
  output s4,
  output s5,
  output s6,
  output s7,
  output c7,
  output c8
);

  wire bit_summator_1_count, bit_summator_2_count, bit_summator_3_count, bit_summator_4_count,
       bit_summator_5_count, bit_summator_6_count;

  bit_summator bit_summator_1 (.a(a0), .b(b0), .cin(c0), .s(s0), .count(bit_summator_1_count));
  bit_summator bit_summator_2 (.a(a1), .b(b1), .cin(bit_summator_1_count), .s(s1), .count(bit_summator_2_count));
  bit_summator bit_summator_3 (.a(a2), .b(b2), .cin(bit_summator_2_count), .s(s2), .count(bit_summator_3_count));
  bit_summator bit_summator_4 (.a(a3), .b(b3), .cin(bit_summator_3_count), .s(s3), .count(bit_summator_4_count));
  bit_summator bit_summator_5 (.a(a4), .b(b4), .cin(bit_summator_4_count), .s(s4), .count(bit_summator_5_count));
  bit_summator bit_summator_6 (.a(a5), .b(b5), .cin(bit_summator_5_count), .s(s5), .count(bit_summator_6_count));
  bit_summator bit_summator_7 (.a(a6), .b(b6), .cin(bit_summator_6_count), .s(s6), .count(c7));
  bit_summator bit_summator_8 (.a(a7), .b(b7), .cin(c7), .s(s7), .count(c8));
endmodule

module bit_summator (
  input  a,
  input  b,
  input  cin,
  output s,
  output count
);

  wire and_1_out, and_2_out, and_3_out;

  ExactlyOne xor_1 (.out(s), .in0(a), .in1(b), .in2(cin));
  and and_1 (and_1_out, b, a);
  and and_2 (and_2_out, cin, a);
  and and_3 (and_3_out, b, cin);
  or or_1 (count, and_1_out, and_2_out, and_3_out);
endmodule

module bit_inverter (
  input  should_change,
  input  \bit ,
  output r
);

  xor xor_1 (r, should_change, \bit );
endmodule

module summator_subtractor (
  input  op,
  input  a0,
  input  a1,
  input  a2,
  input  a3,
  input  a4,
  input  a5,
  input  a6,
  input  a7,
  input  b0,
  input  b1,
  input  b2,
  input  b3,
  input  b4,
  input  b5,
  input  b6,
  input  b7,
  output s0,
  output s1,
  output s2,
  output s3,
  output s4,
  output s5,
  output s6,
  output s7,
  output Overflow
);

  wire bit_inverter_1_r, bit_inverter_2_r, bit_inverter_3_r, bit_inverter_4_r, bit_inverter_5_r,
       bit_inverter_6_r, bit_inverter_7_r, bit_inverter_8_r, summator_1_c8;

  bit_inverter bit_inverter_1 (.should_change(b7), .\bit (b0), .r(bit_inverter_1_r));
  bit_inverter bit_inverter_2 (.should_change(b7), .\bit (b1), .r(bit_inverter_2_r));
  bit_inverter bit_inverter_3 (.should_change(b7), .\bit (b2), .r(bit_inverter_3_r));
  bit_inverter bit_inverter_4 (.should_change(b7), .\bit (b3), .r(bit_inverter_4_r));
  bit_inverter bit_inverter_5 (.should_change(b7), .\bit (b4), .r(bit_inverter_5_r));
  bit_inverter bit_inverter_6 (.should_change(b7), .\bit (b5), .r(bit_inverter_6_r));
  bit_inverter bit_inverter_7 (.should_change(b7), .\bit (b6), .r(bit_inverter_7_r));
  bit_inverter bit_inverter_8 (.should_change(b7), .\bit (b7), .r(bit_inverter_8_r));
  summator summator_1 (
    .a0(a0), .b0(bit_inverter_1_r), .c0(b7), .a1(a1), .b1(bit_inverter_2_r), .a2(a2), .b2(bit_inverter_3_r),
    .a3(a3), .b3(bit_inverter_4_r), .a4(a4), .b4(bit_inverter_5_r), .a5(a5), .b5(bit_inverter_6_r), .a6(a6),
    .b6(bit_inverter_7_r), .a7(a7), .b7(bit_inverter_8_r), .s0(s0), .s1(s1), .s2(s2), .s3(s3), .s4(s4),
    .s5(s5), .s6(s6), .s7(s7), .c8(summator_1_c8));  // open: c7
  xor xor_1 (Overflow, summator_1_c8, b7);

  assign op = b7;
endmodule

module bit_comparator (
  input  a,
  input  b,
  input  c,
  output o_ab973f0b,
  output o_dd94291e,
  output o_8c21dccc
);

  wire and_1_out, and_2_out, not_1_out, not_2_out, not_3_out, xor_1_out;

  xor xor_1 (xor_1_out, a, b);
  and and_1 (and_1_out, a, not_1_out);
  not not_1 (not_1_out, b);
  not not_2 (not_2_out, a);
  not not_3 (not_3_out, xor_1_out);
  and and_2 (and_2_out, not_2_out, b);
  and and_3 (o_ab973f0b, not_3_out, c);
  and and_4 (o_dd94291e, and_1_out, c);
  and and_5 (o_8c21dccc, and_2_out, c);
endmodule

module comparator (
  input  a0,
  input  a1,
  input  a2,
  input  a3,
  input  a4,
  input  a5,
  input  a6,
  input  a7,
  input  b0,
  input  b1,
  input  b2,
  input  b3,
  input  b4,
  input  b5,
  input  b6,
  input  b7,
  output o_ab973f0b,
  output o_dd94291e,
  output o_8c21dccc
);

  wire bit_comparator_1_o_8c21dccc, bit_comparator_1_o_ab973f0b, bit_comparator_1_o_dd94291e,
       bit_comparator_2_o_8c21dccc, bit_comparator_2_o_ab973f0b, bit_comparator_2_o_dd94291e,
       bit_comparator_3_o_8c21dccc, bit_comparator_3_o_ab973f0b, bit_comparator_3_o_dd94291e,
       bit_comparator_4_o_8c21dccc, bit_comparator_4_o_ab973f0b, bit_comparator_4_o_dd94291e,
       bit_comparator_5_o_8c21dccc, bit_comparator_5_o_ab973f0b, bit_comparator_5_o_dd94291e,
       bit_comparator_6_o_8c21dccc, bit_comparator_6_o_ab973f0b, bit_comparator_6_o_dd94291e,
       bit_comparator_7_o_8c21dccc, bit_comparator_7_o_ab973f0b, bit_comparator_7_o_dd94291e,
       bit_comparator_8_o_8c21dccc, bit_comparator_8_o_dd94291e;

  bit_comparator bit_comparator_1 (
    .a(a7), .b(b7), .c(1'b1), .o_ab973f0b(bit_comparator_1_o_ab973f0b),
    .o_dd94291e(bit_comparator_1_o_dd94291e), .o_8c21dccc(bit_comparator_1_o_8c21dccc));
  bit_comparator bit_comparator_2 (
    .a(a6), .b(b6), .c(bit_comparator_1_o_ab973f0b), .o_ab973f0b(bit_comparator_2_o_ab973f0b),
    .o_dd94291e(bit_comparator_2_o_dd94291e), .o_8c21dccc(bit_comparator_2_o_8c21dccc));
  bit_comparator bit_comparator_3 (
    .a(a5), .b(b5), .c(bit_comparator_2_o_ab973f0b), .o_ab973f0b(bit_comparator_3_o_ab973f0b),
    .o_dd94291e(bit_comparator_3_o_dd94291e), .o_8c21dccc(bit_comparator_3_o_8c21dccc));
  bit_comparator bit_comparator_4 (
    .a(a4), .b(b4), .c(bit_comparator_3_o_ab973f0b), .o_ab973f0b(bit_comparator_4_o_ab973f0b),
    .o_dd94291e(bit_comparator_4_o_dd94291e), .o_8c21dccc(bit_comparator_4_o_8c21dccc));
  bit_comparator bit_comparator_5 (
    .a(a3), .b(b3), .c(bit_comparator_4_o_ab973f0b), .o_ab973f0b(bit_comparator_5_o_ab973f0b),
    .o_dd94291e(bit_comparator_5_o_dd94291e), .o_8c21dccc(bit_comparator_5_o_8c21dccc));
  bit_comparator bit_comparator_6 (
    .a(a2), .b(b2), .c(bit_comparator_5_o_ab973f0b), .o_ab973f0b(bit_comparator_6_o_ab973f0b),
    .o_dd94291e(bit_comparator_6_o_dd94291e), .o_8c21dccc(bit_comparator_6_o_8c21dccc));
  bit_comparator bit_comparator_7 (
    .a(a1), .b(b1), .c(bit_comparator_6_o_ab973f0b), .o_ab973f0b(bit_comparator_7_o_ab973f0b),
    .o_dd94291e(bit_comparator_7_o_dd94291e), .o_8c21dccc(bit_comparator_7_o_8c21dccc));
  bit_comparator bit_comparator_8 (
    .a(a0), .b(b0), .c(bit_comparator_7_o_ab973f0b), .o_ab973f0b(o_ab973f0b),
    .o_dd94291e(bit_comparator_8_o_dd94291e), .o_8c21dccc(bit_comparator_8_o_8c21dccc));
  or or_1 (o_dd94291e, bit_comparator_8_o_dd94291e, bit_comparator_7_o_dd94291e, bit_comparator_6_o_dd94291e, bit_comparator_5_o_dd94291e, bit_comparator_4_o_dd94291e, bit_comparator_3_o_dd94291e, bit_comparator_2_o_dd94291e, bit_comparator_1_o_dd94291e);
  or or_2 (o_8c21dccc, bit_comparator_8_o_8c21dccc, bit_comparator_7_o_8c21dccc, bit_comparator_6_o_8c21dccc, bit_comparator_5_o_8c21dccc, bit_comparator_4_o_8c21dccc, bit_comparator_3_o_8c21dccc, bit_comparator_2_o_8c21dccc, bit_comparator_1_o_8c21dccc);
endmodule

module ALU (
  input  OP,
  input  a0,
  input  a1,
  input  a2,
  input  a3,
  input  a4,
  input  a5,
  input  a6,
  input  a7,
  input  b0,
  input  b1,
  input  b2,
  input  b3,
  input  b4,
  input  b5,
  input  b6,
  input  b7,
  output s0,
  output s1,
  output s2,
  output s3,
  output s4,
  output s5,
  output s6,
  output s7,
  output Overflow,
  output o_ab973f0b,
  output o_dd94291e,
  output o_8c21dccc
);

  summator_subtractor summator_subtractor_1 (
    .op(OP), .a0(a0), .a1(a1), .a2(a2), .a3(a3), .a4(a4), .a5(a5), .a6(a6), .a7(a7), .b0(b0), .b1(b1),
    .b2(b2), .b3(b3), .b4(b4), .b5(b5), .b6(b6), .b7(b7), .Overflow(Overflow), .s0(s0), .s1(s1), .s2(s2),
    .s3(s3), .s4(s4), .s5(s5), .s6(s6), .s7(s7));
  comparator comparator_1 (
    .a0(a0), .a1(a1), .a2(a2), .a3(a3), .a4(a4), .a5(a5), .a6(a6), .a7(a7), .b0(b0), .b1(b1), .b2(b2),
    .b3(b3), .b4(b4), .b5(b5), .b6(b6), .b7(b7), .o_ab973f0b(o_ab973f0b), .o_dd94291e(o_dd94291e),
    .o_8c21dccc(o_8c21dccc));
endmodule
